# Fritzing sketch Mapper85_DonkeyKongCountry4VRC7 (saved by Fritzing 1.0.3b)
circuit board: 9.00001cm x 5.68cm
breadboards: 1

parts:
  1-30 = Generic single row SMD female header - 30 pins [form="♀ (female)" package=THT]
  60-31 = Generic single row SMD female header - 30 pins [form="♀ (female)" package=THT]
  3_58MHz = Crystal [frequency="16 Mhz" package=SMD]
  LM358 = LM 358 Dual Op-Amp [package="DIP8 [THT]"]
  LM359 = LM 358 Dual Op-Amp [package="SO 08 [SMD]"]
  27K = Resistor [tolerance=±5% power=0.25W resistance=220 package=THT]
  IC2 = IC, DIP package, 32 pins [chip_label=IC]
  2_2K = Resistor [tolerance=±5% power=0.25W resistance=220 package=THT]
  4_7nF = Ceramic Capacitor [capacitance=100nF voltage=35V package="100 mil [THT, multilayer]"]
  33K = Resistor [tolerance=±5% power=0.25W resistance=220 package=THT]
  1uF = Ceramic Capacitor [capacitance=100nF voltage=35V package="100 mil [THT, multilayer]"]
  22uF = Ceramic Capacitor [capacitance=100nF voltage=35V package="100 mil [THT, multilayer]"]
  4_3K = Resistor [tolerance=±5% power=0.25W resistance=220 package=THT]
  240K = Resistor [tolerance=±5% power=0.25W resistance=220 package=THT]
  910 = Resistor [tolerance=±5% power=0.25W resistance=220 package=THT]
  3_9K = Resistor [tolerance=±5% power=0.25W resistance=220 package=THT]
  2_2K_2 = Resistor [tolerance=±5% power=0.25W resistance=220 package=THT]
  IC3 = IC, DIP package, 32 pins [chip_label=IC]
  VRC7 = IC, DIP package, 48 pins [chip_label=IC]
  Pad1 = Pad [width=1.8450698756469115 height=2.0987357935497952 connect=center]
  Pad2 = Pad [width=1.8450698756469115 height=2.0987357935497952 connect=center]
  Pad3 = Pad [width=1.8450698756469115 height=2.0987357935497952 connect=center]
  18pf = Ceramic Capacitor [capacitance=100nF voltage=35V package="1206 [SMD, multilayer]"]
  18pf1 = Ceramic Capacitor [capacitance=100nF voltage=35V package="1206 [SMD, multilayer]"]

nets:
  N1: 1-30.pin1, IC3.pin16
  N2: 1-30.pin8, VRC7.pin16
  N3: 1-30.pin9, VRC7.pin19
  N4: 1-30.pin16, LM358.connector3, LM359.connector3, 2_2K.Pin_0, 4_7nF.1, 33K.Pin_0, 1uF.0, 22uF.1, 910.Pin_1, VRC7.pin46
  N5: 1-30.pin30, LM358.connector4, LM358.connector5, LM358.connector7, LM359.connector4, LM359.connector5, LM359.connector7, 1uF.1, VRC7.pin42
  N6: 60-31.pin6, VRC7.pin33
  N7: 60-31.pin7, VRC7.pin32
  N8: 60-31.pin8, VRC7.pin31
  N9: 60-31.pin15, 3_9K.Pin_0, 2_2K_2.Pin_1
  N10: 60-31.pin16, 3_9K.Pin_1
  N11: 60-31.pin17, VRC7.pin45
  N12: 60-31.pin18, VRC7.pin7
  N13: 60-31.pin19, VRC7.pin8
  N14: 60-31.pin20, VRC7.pin9
  N15: 60-31.pin21, VRC7.pin10
  N16: 60-31.pin22, VRC7.pin11
  N17: 60-31.pin23, VRC7.pin12
  N18: 60-31.pin24, VRC7.pin13
  N19: 60-31.pin25, VRC7.pin14
  N20: 60-31.pin26, VRC7.pin29
  N21: 60-31.pin27, VRC7.pin28
  N22: 60-31.pin28, VRC7.pin27
  N23: 60-31.pin29, VRC7.pin47
  N24: 3_58MHz.pin_0, VRC7.pin18, Pad3.pad, 18pf1.1
  N25: 3_58MHz.pin_1, VRC7.pin17, Pad1.pad, 18pf.0
  N26: LM358.connector0, LM359.connector0, 240K.Pin_1, 910.Pin_0, 2_2K_2.Pin_0
  N27: LM358.connector1, LM359.connector1, 4_3K.Pin_0, 240K.Pin_0
  N28: LM358.connector2, LM359.connector2, 27K.Pin_0, 4_7nF.0, 33K.Pin_1
  N29: LM358.connector6, LM359.connector6
  N30: 27K.Pin_1, 2_2K.Pin_1, VRC7.pin43
  N31: IC2.pin2, VRC7.pin40
  N32: IC2.pin3, VRC7.pin39
  N33: IC2.pin4, VRC7.pin36
  N34: IC2.pin23, VRC7.pin34
  N35: IC2.pin25, VRC7.pin35
  N36: IC2.pin28, VRC7.pin37
  N37: IC2.pin29, VRC7.pin38
  N38: IC2.pin30, VRC7.pin41
  N39: 22uF.0, 4_3K.Pin_1
  N40: IC3.pin2, VRC7.pin23
  N41: IC3.pin3, VRC7.pin22
  N42: IC3.pin22, VRC7.pin44
  N43: IC3.pin28, VRC7.pin20
  N44: IC3.pin29, VRC7.pin21
  N45: IC3.pin30, VRC7.pin25
  N46: IC3.pin31, VRC7.pin26
  N47: Pad2.pad, 18pf.1, 18pf1.0

notes:
  4 VRC7 Hack Repro PCB
  Designed by HeeminYT
  If you're going to
  use oscillator,
  fi ll two capacitors above,
  if you're going to use
  use resonator instead,
  just place it on
  the three contacts on the top
  ^ the debug pin

custom parts:
  Generic single row SMD female header - 30 pins: Generic single row SMD female header
