# Fritzing sketch ShuiGuanPipe (saved by Fritzing 0.9.3b)
circuit board: 9.00001cm x 5.68cm
breadboards: 1

parts:
  J2 = Generic single row SMD female header - 30 pins [form="♀ (female)" package=THT]
  J3 = Generic single row SMD female header - 30 pins [form="♀ (female)" package=THT]  # not connected
  D1 = Rectifier Diode [part_number=1N4001 package="300 mil [THT]"]
  1_8K = Resistor [tolerance=±5% resistance=220 package=THT]
  74LS161 = IC, DIP package, 16 pins [chip_label=IC]
  74LS157 = IC, DIP package, 16 pins [chip_label=IC]
  74LS157_2 = IC, DIP package, 16 pins [chip_label=IC]
  AX5208C_/_VRC4 = IC, DIP package, 40 pins [chip_label=IC]
  100p = Ceramic Capacitor [capacitance=100nF package="200 mil [THT, multilayer]"]
  27C1 = 27C020 EEPROM [chip_label=27C020 package="DIP (Dual Inline) [THT]"]  # not connected

nets:
  N1: J2.pin14, 74LS161.pin9, AX5208C_/_VRC4.pin9
  N2: J2.pin15, AX5208C_/_VRC4.pin17
  N3: J2.pin17, AX5208C_/_VRC4.pin12
  N4: J2.pin18, AX5208C_/_VRC4.pin13
  N5: D1.cathode, 1_8K.Pin_0, 74LS161.pin2, 100p.1
  N6: D1.anode, 1_8K.Pin_1, 74LS157_2.pin10, AX5208C_/_VRC4.pin19
  N7: 74LS161.pin5, AX5208C_/_VRC4.pin4
  N8: 74LS161.pin6, AX5208C_/_VRC4.pin3
  N9: 74LS161.pin7, 74LS161.pin10, 74LS157.pin13, 74LS157.pin16, 74LS157_2.pin6, 74LS157_2.pin15, 100p.0
  N10: 74LS161.pin11, 74LS157_2.pin3
  N11: 74LS161.pin12, 74LS157.pin10
  N12: 74LS161.pin13, 74LS157.pin6
  N13: 74LS161.pin14, 74LS157.pin3
  N14: 74LS157.pin2, AX5208C_/_VRC4.pin35
  N15: 74LS157.pin5, AX5208C_/_VRC4.pin36
  N16: 74LS157.pin11, AX5208C_/_VRC4.pin38
  N17: 74LS157.pin12, AX5208C_/_VRC4.pin37
  N18: 74LS157_2.pin2, AX5208C_/_VRC4.pin34
  N19: 74LS157_2.pin5, AX5208C_/_VRC4.pin39
  N20: 74LS157_2.pin11, AX5208C_/_VRC4.pin8

notes:
  水管PIPE
  wtf??

custom parts:
  Generic single row SMD female header - 30 pins: Generic single row SMD female header
  27C020 EEPROM: An EPROM (rarely EROM), or erasable programmable read-only memory, is a type of programmable read-only memory (PROM) chip that retains its data when its power supply is switched off.
